// Logisim project ALU.circ as structural Verilog: 9 circuits, main circuit Half-Adder
// HA
module Half_Adder (
  input  A,
  input  B,
  output S,
  output C
);

  xor xor_1 (S, A, B);
  and and_1 (C, A, B);

  // Notes on the sheet:
  //   Half-Adder Circuit Design
  //   S(A, B) = A ^ B
  //   C(A, B) = AB
endmodule

// FA
module Full_Adder (
  input  A,
  input  B,
  input  C_in,
  output C_out,
  output S
);

  wire half_adder_1_c, half_adder_1_s, half_adder_2_c;

  Half_Adder half_adder_1 (.A(A), .B(B), .S(half_adder_1_s), .C(half_adder_1_c));
  Half_Adder half_adder_2 (.A(half_adder_1_s), .B(C_in), .S(S), .C(half_adder_2_c));
  or or_1 (C_out, half_adder_1_c, half_adder_2_c);

  // Notes on the sheet:
  //   Full-Adder Circuit Design
  //   S(A, B, C_in) = HA.S(HA.S(A,B), C_in)
  //   C_out(A, B, C_in) = HA.C(A, B) + HA.C(HA.S(A, B), C_in)
endmodule

module Overflow (
  input  C_k_2,
  input  C_k_1,
  output Overflow
);

  wire xor_1_out;

  xor xor_1 (xor_1_out, C_k_2, C_k_1);
  or or_1 (Overflow, xor_1_out, C_k_1);

  // Notes on the sheet:
  //   Overflow Logic Circuit Design
  //   2C Overflow
  //   Unsigned Overflow
  //   Overflow(C_k-2, C_k-1) = (C_k-2 ^ C_k-1) + C_k-1
endmodule

// 1b ALU
module _1_bit_ALU (
  input  A_inv,
  input  B_inv,
  input  C_in,
  input  [1:0] Op,
  input  A,
  input  B,
  input  Less,
  output Result,
  output Set,
  output C_out
);

  wire and_1_out, multiplexer_1_out, multiplexer_2_out, not_1_out, not_2_out, or_1_out;

  not not_1 (not_1_out, A);
  not not_2 (not_2_out, B);
  Multiplexer #(.enable("false")) multiplexer_1 (.in0(A), .in1(not_1_out), .out(multiplexer_1_out), .sel(A_inv));
  Multiplexer #(.enable("false")) multiplexer_2 (.in0(B), .in1(not_2_out), .out(multiplexer_2_out), .sel(B_inv));
  and and_1 (and_1_out, multiplexer_1_out, multiplexer_2_out);
  or or_1 (or_1_out, multiplexer_1_out, multiplexer_2_out);
  Full_Adder full_adder_1 (.A(multiplexer_1_out), .B(multiplexer_2_out), .C_in(C_in), .C_out(C_out), .S(Set));
  Multiplexer #(.select(2), .enable("false")) multiplexer_3 (
    .in0(and_1_out), .in1(or_1_out), .in2(Set), .in3(Less), .out(Result), .sel(Op));

  // Notes on the sheet:
  //   1-bit ALU Design
endmodule

// 2b ALU
module _2_bit_ALU (
  input  A_inv,
  input  B_inv,
  input  [1:0] Op,
  input  [1:0] A,
  input  [1:0] B,
  output Zero,
  output [1:0] Result,
  output Overflow
);

  wire n1_bit_alu_1_c_out, n1_bit_alu_2_c_out, n1_bit_alu_2_set;

  _1_bit_ALU u_1_bit_alu_1 (
    .A(A[0]), .B(B[0]), .Less(n1_bit_alu_2_set), .Result(Result[0]), .A_inv(A_inv), .B_inv(B_inv),
    .C_in(B_inv), .Op(Op), .C_out(n1_bit_alu_1_c_out));  // open: Set
  _1_bit_ALU u_1_bit_alu_2 (
    .A(A[1]), .B(B[1]), .Less(1'b0), .Result(Result[1]), .A_inv(A_inv), .B_inv(B_inv),
    .C_in(n1_bit_alu_1_c_out), .Op(Op), .Set(n1_bit_alu_2_set), .C_out(n1_bit_alu_2_c_out));
  Overflow overflow_1 (.C_k_2(n1_bit_alu_1_c_out), .C_k_1(n1_bit_alu_2_c_out), .Overflow(Overflow));
  nor nor_1 (Zero, Result[0], Result[1]);

  // Notes on the sheet:
  //   Result
  //   Zero
  //   2-bit ALU Design
  //   Overflow (2C, U)
endmodule

// 4b ALU
module _4_bit_ALU (
  input  A_inv,
  input  B_inv,
  input  [1:0] Op,
  input  [3:0] A,
  input  [3:0] B,
  output Zero,
  output [3:0] Result,
  output Overflow
);

  wire n1_bit_alu_1_c_out, n1_bit_alu_2_c_out, n1_bit_alu_3_c_out, n1_bit_alu_4_c_out, n1_bit_alu_4_set;

  _1_bit_ALU u_1_bit_alu_1 (
    .A(A[0]), .B(B[0]), .Less(n1_bit_alu_4_set), .Result(Result[0]), .A_inv(A_inv), .B_inv(B_inv),
    .C_in(B_inv), .Op(Op), .C_out(n1_bit_alu_1_c_out));  // open: Set
  _1_bit_ALU u_1_bit_alu_2 (
    .A(A[1]), .B(B[1]), .Less(1'b0), .Result(Result[1]), .A_inv(A_inv), .B_inv(B_inv),
    .C_in(n1_bit_alu_1_c_out), .Op(Op), .C_out(n1_bit_alu_2_c_out));  // open: Set
  _1_bit_ALU u_1_bit_alu_3 (
    .A(A[2]), .B(B[2]), .Less(1'b0), .Result(Result[2]), .A_inv(A_inv), .B_inv(B_inv),
    .C_in(n1_bit_alu_2_c_out), .Op(Op), .C_out(n1_bit_alu_3_c_out));  // open: Set
  _1_bit_ALU u_1_bit_alu_4 (
    .A(A[3]), .B(B[3]), .Less(1'b0), .Result(Result[3]), .A_inv(A_inv), .B_inv(B_inv),
    .C_in(n1_bit_alu_3_c_out), .Op(Op), .Set(n1_bit_alu_4_set), .C_out(n1_bit_alu_4_c_out));
  Overflow overflow_1 (.C_k_2(n1_bit_alu_3_c_out), .C_k_1(n1_bit_alu_4_c_out), .Overflow(Overflow));
  nor nor_1 (Zero, Result[0], Result[1], Result[2], Result[3]);

  // Notes on the sheet:
  //   4-bit ALU Design
endmodule

// 8b ALU
module _8_bit_ALU (
  input  A_inv,
  input  B_inv,
  input  [1:0] Op,
  input  [7:0] A,
  input  [7:0] B,
  output Zero,
  output [7:0] Result,
  output Overflow
);

  wire n1_bit_alu_1_c_out, n1_bit_alu_2_c_out, n1_bit_alu_3_c_out, n1_bit_alu_4_c_out, n1_bit_alu_5_c_out,
       n1_bit_alu_6_c_out, n1_bit_alu_7_c_out, n1_bit_alu_8_c_out, n1_bit_alu_8_set;

  _1_bit_ALU u_1_bit_alu_1 (
    .A(A[0]), .B(B[0]), .Less(n1_bit_alu_8_set), .Result(Result[0]), .A_inv(A_inv), .B_inv(B_inv), .Op(Op),
    .C_out(n1_bit_alu_1_c_out));  // open: C_in, Set
  _1_bit_ALU u_1_bit_alu_2 (
    .A(A[2]), .B(B[2]), .Less(1'b0), .Result(Result[2]), .A_inv(A_inv), .B_inv(B_inv),
    .C_in(n1_bit_alu_5_c_out), .Op(Op), .C_out(n1_bit_alu_2_c_out));  // open: Set
  _1_bit_ALU u_1_bit_alu_3 (
    .A(A[4]), .B(B[4]), .Less(1'b0), .Result(Result[4]), .A_inv(A_inv), .B_inv(B_inv),
    .C_in(n1_bit_alu_6_c_out), .Op(Op), .C_out(n1_bit_alu_3_c_out));  // open: Set
  _1_bit_ALU u_1_bit_alu_4 (
    .A(A[6]), .B(B[6]), .Less(1'b0), .Result(Result[6]), .A_inv(A_inv), .B_inv(B_inv),
    .C_in(n1_bit_alu_7_c_out), .Op(Op), .C_out(n1_bit_alu_4_c_out));  // open: Set
  _1_bit_ALU u_1_bit_alu_5 (
    .A(A[1]), .B(B[1]), .Less(1'b0), .Result(Result[1]), .A_inv(A_inv), .B_inv(B_inv),
    .C_in(n1_bit_alu_1_c_out), .Op(Op), .C_out(n1_bit_alu_5_c_out));  // open: Set
  _1_bit_ALU u_1_bit_alu_6 (
    .A(A[3]), .B(B[3]), .Less(1'b0), .Result(Result[3]), .A_inv(A_inv), .B_inv(B_inv),
    .C_in(n1_bit_alu_2_c_out), .Op(Op), .C_out(n1_bit_alu_6_c_out));  // open: Set
  _1_bit_ALU u_1_bit_alu_7 (
    .A(A[5]), .B(B[5]), .Less(1'b0), .Result(Result[5]), .A_inv(A_inv), .B_inv(B_inv),
    .C_in(n1_bit_alu_3_c_out), .Op(Op), .C_out(n1_bit_alu_7_c_out));  // open: Set
  _1_bit_ALU u_1_bit_alu_8 (
    .A(A[7]), .B(B[7]), .Less(1'b0), .Result(Result[7]), .A_inv(A_inv), .B_inv(B_inv),
    .C_in(n1_bit_alu_4_c_out), .Op(Op), .Set(n1_bit_alu_8_set), .C_out(n1_bit_alu_8_c_out));
  Overflow overflow_1 (.C_k_2(n1_bit_alu_4_c_out), .C_k_1(n1_bit_alu_8_c_out), .Overflow(Overflow));
  nor nor_1 (Zero, Result[0], Result[1], Result[2], Result[3], Result[4], Result[5], Result[6], Result[7]);

  // Notes on the sheet:
  //   8-bit ALU Design
endmodule

// 16b ALU
module _16_bit_ALU (
  input  A_inv,
  input  B_inv,
  input  [1:0] Op,
  input  [15:0] A,
  input  [15:0] B,
  output Zero,
  output [15:0] Result,
  output Overflow
);

  wire n1_bit_alu_1_c_out, n1_bit_alu_2_c_out, n1_bit_alu_3_c_out, n1_bit_alu_4_c_out, n1_bit_alu_5_c_out,
       n1_bit_alu_6_c_out, n1_bit_alu_7_c_out, n1_bit_alu_8_c_out, n1_bit_alu_9_c_out, n1_bit_alu_10_c_out,
       n1_bit_alu_11_c_out, n1_bit_alu_12_c_out, n1_bit_alu_13_c_out, n1_bit_alu_14_c_out,
       n1_bit_alu_15_c_out, n1_bit_alu_16_c_out, n1_bit_alu_16_set;

  _1_bit_ALU u_1_bit_alu_1 (
    .A(A[0]), .B(B[0]), .Less(n1_bit_alu_16_set), .Result(Result[0]), .A_inv(A_inv), .B_inv(B_inv),
    .C_in(B_inv), .Op(Op), .C_out(n1_bit_alu_1_c_out));  // open: Set
  _1_bit_ALU u_1_bit_alu_2 (
    .A(A[2]), .B(B[2]), .Less(1'b0), .Result(Result[2]), .A_inv(A_inv), .B_inv(B_inv),
    .C_in(n1_bit_alu_5_c_out), .Op(Op), .C_out(n1_bit_alu_2_c_out));  // open: Set
  _1_bit_ALU u_1_bit_alu_3 (
    .A(A[4]), .B(B[4]), .Less(1'b0), .Result(Result[4]), .A_inv(A_inv), .B_inv(B_inv),
    .C_in(n1_bit_alu_6_c_out), .Op(Op), .C_out(n1_bit_alu_3_c_out));  // open: Set
  _1_bit_ALU u_1_bit_alu_4 (
    .A(A[6]), .B(B[6]), .Less(1'b0), .Result(Result[6]), .A_inv(A_inv), .B_inv(B_inv),
    .C_in(n1_bit_alu_7_c_out), .Op(Op), .C_out(n1_bit_alu_4_c_out));  // open: Set
  _1_bit_ALU u_1_bit_alu_5 (
    .A(A[1]), .B(B[1]), .Less(1'b0), .Result(Result[1]), .A_inv(A_inv), .B_inv(B_inv),
    .C_in(n1_bit_alu_1_c_out), .Op(Op), .C_out(n1_bit_alu_5_c_out));  // open: Set
  _1_bit_ALU u_1_bit_alu_6 (
    .A(A[3]), .B(B[3]), .Less(1'b0), .Result(Result[3]), .A_inv(A_inv), .B_inv(B_inv),
    .C_in(n1_bit_alu_2_c_out), .Op(Op), .C_out(n1_bit_alu_6_c_out));  // open: Set
  _1_bit_ALU u_1_bit_alu_7 (
    .A(A[5]), .B(B[5]), .Less(1'b0), .Result(Result[5]), .A_inv(A_inv), .B_inv(B_inv),
    .C_in(n1_bit_alu_3_c_out), .Op(Op), .C_out(n1_bit_alu_7_c_out));  // open: Set
  _1_bit_ALU u_1_bit_alu_8 (
    .A(A[7]), .B(B[7]), .Less(1'b0), .Result(Result[7]), .A_inv(A_inv), .B_inv(B_inv),
    .C_in(n1_bit_alu_4_c_out), .Op(Op), .C_out(n1_bit_alu_8_c_out));  // open: Set
  _1_bit_ALU u_1_bit_alu_9 (
    .A(A[8]), .B(B[8]), .Less(1'b0), .Result(Result[8]), .A_inv(A_inv), .B_inv(B_inv),
    .C_in(n1_bit_alu_8_c_out), .Op(Op), .C_out(n1_bit_alu_9_c_out));  // open: Set
  _1_bit_ALU u_1_bit_alu_10 (
    .A(A[10]), .B(B[10]), .Less(1'b0), .Result(Result[10]), .A_inv(A_inv), .B_inv(B_inv),
    .C_in(n1_bit_alu_13_c_out), .Op(Op), .C_out(n1_bit_alu_10_c_out));  // open: Set
  _1_bit_ALU u_1_bit_alu_11 (
    .A(A[12]), .B(B[12]), .Less(1'b0), .Result(Result[12]), .A_inv(A_inv), .B_inv(B_inv),
    .C_in(n1_bit_alu_14_c_out), .Op(Op), .C_out(n1_bit_alu_11_c_out));  // open: Set
  _1_bit_ALU u_1_bit_alu_12 (
    .A(A[14]), .B(B[14]), .Less(1'b0), .Result(Result[14]), .A_inv(A_inv), .B_inv(B_inv),
    .C_in(n1_bit_alu_15_c_out), .Op(Op), .C_out(n1_bit_alu_12_c_out));  // open: Set
  _1_bit_ALU u_1_bit_alu_13 (
    .A(A[9]), .B(B[9]), .Less(1'b0), .Result(Result[9]), .A_inv(A_inv), .B_inv(B_inv),
    .C_in(n1_bit_alu_9_c_out), .Op(Op), .C_out(n1_bit_alu_13_c_out));  // open: Set
  _1_bit_ALU u_1_bit_alu_14 (
    .A(A[11]), .B(B[11]), .Less(1'b0), .Result(Result[11]), .A_inv(A_inv), .B_inv(B_inv),
    .C_in(n1_bit_alu_10_c_out), .Op(Op), .C_out(n1_bit_alu_14_c_out));  // open: Set
  _1_bit_ALU u_1_bit_alu_15 (
    .A(A[13]), .B(B[13]), .Less(1'b0), .Result(Result[13]), .A_inv(A_inv), .B_inv(B_inv),
    .C_in(n1_bit_alu_11_c_out), .Op(Op), .C_out(n1_bit_alu_15_c_out));  // open: Set
  _1_bit_ALU u_1_bit_alu_16 (
    .A(A[15]), .B(B[15]), .Less(1'b0), .Result(Result[15]), .A_inv(A_inv), .B_inv(B_inv),
    .C_in(n1_bit_alu_12_c_out), .Op(Op), .Set(n1_bit_alu_16_set), .C_out(n1_bit_alu_16_c_out));
  Overflow overflow_1 (.C_k_2(n1_bit_alu_12_c_out), .C_k_1(n1_bit_alu_16_c_out), .Overflow(Overflow));
  nor nor_1 (Zero, Result[0], Result[1], Result[2], Result[3], Result[4], Result[5], Result[6], Result[7], Result[8], Result[9], Result[10], Result[11], Result[12], Result[13], Result[14], Result[15]);

  // Notes on the sheet:
  //   16-bit ALU Design
endmodule

// 32b ALU
module _32_bit_ALU (
  input  [3:0] Op,
  input  [31:0] A,
  input  [31:0] B,
  output Zero,
  output [31:0] Result,
  output Overflow,
  output C_out
);

  wire n1_bit_alu_1_c_out, n1_bit_alu_2_c_out, n1_bit_alu_3_c_out, n1_bit_alu_4_c_out, n1_bit_alu_5_c_out,
       n1_bit_alu_6_c_out, n1_bit_alu_7_c_out, n1_bit_alu_8_c_out, n1_bit_alu_9_c_out, n1_bit_alu_10_c_out,
       n1_bit_alu_11_c_out, n1_bit_alu_12_c_out, n1_bit_alu_13_c_out, n1_bit_alu_14_c_out,
       n1_bit_alu_15_c_out, n1_bit_alu_16_set, n1_bit_alu_17_c_out, n1_bit_alu_18_c_out, n1_bit_alu_19_c_out,
       n1_bit_alu_20_c_out, n1_bit_alu_21_c_out, n1_bit_alu_22_c_out, n1_bit_alu_23_c_out,
       n1_bit_alu_24_c_out, n1_bit_alu_25_c_out, n1_bit_alu_26_c_out, n1_bit_alu_27_c_out,
       n1_bit_alu_28_c_out, n1_bit_alu_29_c_out, n1_bit_alu_30_c_out, n1_bit_alu_31_c_out,
       n1_bit_alu_32_c_out;

  _1_bit_ALU u_1_bit_alu_1 (
    .A(A[0]), .B(B[0]), .Less(n1_bit_alu_16_set), .Result(Result[0]), .A_inv(Op[3]), .B_inv(Op[2]),
    .C_in(Op[2]), .Op(Op[1:0]), .C_out(n1_bit_alu_1_c_out));  // open: Set
  _1_bit_ALU u_1_bit_alu_2 (
    .A(A[2]), .B(B[2]), .Less(1'b0), .Result(Result[2]), .A_inv(Op[3]), .B_inv(Op[2]),
    .C_in(n1_bit_alu_5_c_out), .Op(Op[1:0]), .C_out(n1_bit_alu_2_c_out));  // open: Set
  _1_bit_ALU u_1_bit_alu_3 (
    .A(A[4]), .B(B[4]), .Less(1'b0), .Result(Result[4]), .A_inv(Op[3]), .B_inv(Op[2]),
    .C_in(n1_bit_alu_6_c_out), .Op(Op[1:0]), .C_out(n1_bit_alu_3_c_out));  // open: Set
  _1_bit_ALU u_1_bit_alu_4 (
    .A(A[6]), .B(B[6]), .Less(1'b0), .Result(Result[6]), .A_inv(Op[3]), .B_inv(Op[2]),
    .C_in(n1_bit_alu_7_c_out), .Op(Op[1:0]), .C_out(n1_bit_alu_4_c_out));  // open: Set
  _1_bit_ALU u_1_bit_alu_5 (
    .A(A[1]), .B(B[1]), .Less(1'b0), .Result(Result[1]), .A_inv(Op[3]), .B_inv(Op[2]),
    .C_in(n1_bit_alu_1_c_out), .Op(Op[1:0]), .C_out(n1_bit_alu_5_c_out));  // open: Set
  _1_bit_ALU u_1_bit_alu_6 (
    .A(A[3]), .B(B[3]), .Less(1'b0), .Result(Result[3]), .A_inv(Op[3]), .B_inv(Op[2]),
    .C_in(n1_bit_alu_2_c_out), .Op(Op[1:0]), .C_out(n1_bit_alu_6_c_out));  // open: Set
  _1_bit_ALU u_1_bit_alu_7 (
    .A(A[5]), .B(B[5]), .Less(1'b0), .Result(Result[5]), .A_inv(Op[3]), .B_inv(Op[2]),
    .C_in(n1_bit_alu_3_c_out), .Op(Op[1:0]), .C_out(n1_bit_alu_7_c_out));  // open: Set
  _1_bit_ALU u_1_bit_alu_8 (
    .A(A[7]), .B(B[7]), .Less(1'b0), .Result(Result[7]), .A_inv(Op[3]), .B_inv(Op[2]),
    .C_in(n1_bit_alu_4_c_out), .Op(Op[1:0]), .C_out(n1_bit_alu_8_c_out));  // open: Set
  _1_bit_ALU u_1_bit_alu_9 (
    .A(A[24]), .B(B[24]), .Less(1'b0), .Result(Result[24]), .A_inv(Op[3]), .B_inv(Op[2]),
    .C_in(n1_bit_alu_32_c_out), .Op(Op[1:0]), .C_out(n1_bit_alu_9_c_out));  // open: Set
  _1_bit_ALU u_1_bit_alu_10 (
    .A(A[26]), .B(B[26]), .Less(1'b0), .Result(Result[26]), .A_inv(Op[3]), .B_inv(Op[2]),
    .C_in(n1_bit_alu_13_c_out), .Op(Op[1:0]), .C_out(n1_bit_alu_10_c_out));  // open: Set
  _1_bit_ALU u_1_bit_alu_11 (
    .A(A[28]), .B(B[28]), .Less(1'b0), .Result(Result[28]), .A_inv(Op[3]), .B_inv(Op[2]),
    .C_in(n1_bit_alu_14_c_out), .Op(Op[1:0]), .C_out(n1_bit_alu_11_c_out));  // open: Set
  _1_bit_ALU u_1_bit_alu_12 (
    .A(A[30]), .B(B[30]), .Less(1'b0), .Result(Result[30]), .A_inv(Op[3]), .B_inv(Op[2]),
    .C_in(n1_bit_alu_15_c_out), .Op(Op[1:0]), .C_out(n1_bit_alu_12_c_out));  // open: Set
  _1_bit_ALU u_1_bit_alu_13 (
    .A(A[25]), .B(B[25]), .Less(1'b0), .Result(Result[25]), .A_inv(Op[3]), .B_inv(Op[2]),
    .C_in(n1_bit_alu_9_c_out), .Op(Op[1:0]), .C_out(n1_bit_alu_13_c_out));  // open: Set
  _1_bit_ALU u_1_bit_alu_14 (
    .A(A[27]), .B(B[27]), .Less(1'b0), .Result(Result[27]), .A_inv(Op[3]), .B_inv(Op[2]),
    .C_in(n1_bit_alu_10_c_out), .Op(Op[1:0]), .C_out(n1_bit_alu_14_c_out));  // open: Set
  _1_bit_ALU u_1_bit_alu_15 (
    .A(A[29]), .B(B[29]), .Less(1'b0), .Result(Result[29]), .A_inv(Op[3]), .B_inv(Op[2]),
    .C_in(n1_bit_alu_11_c_out), .Op(Op[1:0]), .C_out(n1_bit_alu_15_c_out));  // open: Set
  _1_bit_ALU u_1_bit_alu_16 (
    .A(A[31]), .B(B[31]), .Less(1'b0), .Result(Result[31]), .A_inv(Op[3]), .B_inv(Op[2]),
    .C_in(n1_bit_alu_12_c_out), .Op(Op[1:0]), .Set(n1_bit_alu_16_set), .C_out(C_out));
  _1_bit_ALU u_1_bit_alu_17 (
    .A(A[8]), .B(B[8]), .Less(1'b0), .Result(Result[8]), .A_inv(Op[3]), .B_inv(Op[2]),
    .C_in(n1_bit_alu_8_c_out), .Op(Op[1:0]), .C_out(n1_bit_alu_17_c_out));  // open: Set
  _1_bit_ALU u_1_bit_alu_18 (
    .A(A[10]), .B(B[10]), .Less(1'b0), .Result(Result[10]), .A_inv(Op[3]), .B_inv(Op[2]),
    .C_in(n1_bit_alu_21_c_out), .Op(Op[1:0]), .C_out(n1_bit_alu_18_c_out));  // open: Set
  _1_bit_ALU u_1_bit_alu_19 (
    .A(A[12]), .B(B[12]), .Less(1'b0), .Result(Result[12]), .A_inv(Op[3]), .B_inv(Op[2]),
    .C_in(n1_bit_alu_22_c_out), .Op(Op[1:0]), .C_out(n1_bit_alu_19_c_out));  // open: Set
  _1_bit_ALU u_1_bit_alu_20 (
    .A(A[14]), .B(B[14]), .Less(1'b0), .Result(Result[14]), .A_inv(Op[3]), .B_inv(Op[2]),
    .C_in(n1_bit_alu_23_c_out), .Op(Op[1:0]), .C_out(n1_bit_alu_20_c_out));  // open: Set
  _1_bit_ALU u_1_bit_alu_21 (
    .A(A[9]), .B(B[9]), .Less(1'b0), .Result(Result[9]), .A_inv(Op[3]), .B_inv(Op[2]),
    .C_in(n1_bit_alu_17_c_out), .Op(Op[1:0]), .C_out(n1_bit_alu_21_c_out));  // open: Set
  _1_bit_ALU u_1_bit_alu_22 (
    .A(A[11]), .B(B[11]), .Less(1'b0), .Result(Result[11]), .A_inv(Op[3]), .B_inv(Op[2]),
    .C_in(n1_bit_alu_18_c_out), .Op(Op[1:0]), .C_out(n1_bit_alu_22_c_out));  // open: Set
  _1_bit_ALU u_1_bit_alu_23 (
    .A(A[13]), .B(B[13]), .Less(1'b0), .Result(Result[13]), .A_inv(Op[3]), .B_inv(Op[2]),
    .C_in(n1_bit_alu_19_c_out), .Op(Op[1:0]), .C_out(n1_bit_alu_23_c_out));  // open: Set
  _1_bit_ALU u_1_bit_alu_24 (
    .A(A[15]), .B(B[15]), .Less(1'b0), .Result(Result[15]), .A_inv(Op[3]), .B_inv(Op[2]),
    .C_in(n1_bit_alu_20_c_out), .Op(Op[1:0]), .C_out(n1_bit_alu_24_c_out));  // open: Set
  _1_bit_ALU u_1_bit_alu_25 (
    .A(A[16]), .B(B[16]), .Less(1'b0), .Result(Result[16]), .A_inv(Op[3]), .B_inv(Op[2]),
    .C_in(n1_bit_alu_24_c_out), .Op(Op[1:0]), .C_out(n1_bit_alu_25_c_out));  // open: Set
  _1_bit_ALU u_1_bit_alu_26 (
    .A(A[18]), .B(B[18]), .Less(1'b0), .Result(Result[18]), .A_inv(Op[3]), .B_inv(Op[2]),
    .C_in(n1_bit_alu_29_c_out), .Op(Op[1:0]), .C_out(n1_bit_alu_26_c_out));  // open: Set
  _1_bit_ALU u_1_bit_alu_27 (
    .A(A[20]), .B(B[20]), .Less(1'b0), .Result(Result[20]), .A_inv(Op[3]), .B_inv(Op[2]),
    .C_in(n1_bit_alu_30_c_out), .Op(Op[1:0]), .C_out(n1_bit_alu_27_c_out));  // open: Set
  _1_bit_ALU u_1_bit_alu_28 (
    .A(A[22]), .B(B[22]), .Less(1'b0), .Result(Result[22]), .A_inv(Op[3]), .B_inv(Op[2]),
    .C_in(n1_bit_alu_31_c_out), .Op(Op[1:0]), .C_out(n1_bit_alu_28_c_out));  // open: Set
  _1_bit_ALU u_1_bit_alu_29 (
    .A(A[17]), .B(B[17]), .Less(1'b0), .Result(Result[17]), .A_inv(Op[3]), .B_inv(Op[2]),
    .C_in(n1_bit_alu_25_c_out), .Op(Op[1:0]), .C_out(n1_bit_alu_29_c_out));  // open: Set
  _1_bit_ALU u_1_bit_alu_30 (
    .A(A[19]), .B(B[19]), .Less(1'b0), .Result(Result[19]), .A_inv(Op[3]), .B_inv(Op[2]),
    .C_in(n1_bit_alu_26_c_out), .Op(Op[1:0]), .C_out(n1_bit_alu_30_c_out));  // open: Set
  _1_bit_ALU u_1_bit_alu_31 (
    .A(A[21]), .B(B[21]), .Less(1'b0), .Result(Result[21]), .A_inv(Op[3]), .B_inv(Op[2]),
    .C_in(n1_bit_alu_27_c_out), .Op(Op[1:0]), .C_out(n1_bit_alu_31_c_out));  // open: Set
  _1_bit_ALU u_1_bit_alu_32 (
    .A(A[23]), .B(B[23]), .Less(1'b0), .Result(Result[23]), .A_inv(Op[3]), .B_inv(Op[2]),
    .C_in(n1_bit_alu_28_c_out), .Op(Op[1:0]), .C_out(n1_bit_alu_32_c_out));  // open: Set
  Overflow overflow_1 (.C_k_2(n1_bit_alu_12_c_out), .C_k_1(C_out), .Overflow(Overflow));
  nor nor_1 (Zero, Result[0], Result[1], Result[2], Result[3], Result[4], Result[5], Result[6], Result[7], Result[8], Result[9], Result[10], Result[11], Result[12], Result[13], Result[14], Result[15], Result[16], Result[17], Result[18], Result[19], Result[20], Result[21], Result[22], Result[23], Result[24], Result[25], Result[26], Result[27], Result[28], Result[29], Result[30], Result[31]);

  // Notes on the sheet:
  //   32-bit ALU Design
endmodule
