// Logisim project Registers.circ as structural Verilog
// dff
module D_Flip_Flop (
  input  D,
  input  clk,
  output Q,
  output Q_prime
);

  wire nand_1_out, nand_2_out, not_1_out;

  not not_1 (not_1_out, D);
  nand nand_1 (nand_1_out, D, clk);
  nand nand_2 (nand_2_out, not_1_out, clk);
  nand nand_3 (Q, nand_1_out, Q_prime);
  nand nand_4 (Q_prime, Q, nand_2_out);
endmodule

// Reg[0:31]
module Register (
  input  Write,
  input  clk,
  input  [31:0] Input
);

  wire d_flip_flop_1_q, d_flip_flop_2_q, d_flip_flop_3_q, d_flip_flop_4_q, d_flip_flop_5_q, d_flip_flop_6_q,
       d_flip_flop_7_q, d_flip_flop_8_q, d_flip_flop_9_q, d_flip_flop_10_q, d_flip_flop_11_q,
       d_flip_flop_12_q, d_flip_flop_13_q, d_flip_flop_14_q, d_flip_flop_15_q, d_flip_flop_16_q,
       d_flip_flop_17_q, d_flip_flop_18_q, d_flip_flop_19_q, d_flip_flop_20_q, d_flip_flop_21_p2,
       d_flip_flop_21_p3, d_flip_flop_22_q, d_flip_flop_23_q, d_flip_flop_24_q, d_flip_flop_25_q,
       d_flip_flop_26_q, d_flip_flop_27_q, d_flip_flop_28_q, d_flip_flop_29_q, d_flip_flop_30_q,
       d_flip_flop_31_q, d_flip_flop_32_q, multiplexer_1_out, multiplexer_2_out, multiplexer_3_out,
       multiplexer_4_out, multiplexer_5_out, multiplexer_6_out, multiplexer_7_out, multiplexer_8_out,
       multiplexer_9_out, multiplexer_10_out, multiplexer_11_out, multiplexer_12_out, multiplexer_13_out,
       multiplexer_14_out, multiplexer_15_out, multiplexer_16_out, multiplexer_17_out, multiplexer_18_out,
       multiplexer_19_out, multiplexer_20_out, multiplexer_21_out, multiplexer_22_out, multiplexer_23_out,
       multiplexer_24_out, multiplexer_25_out, multiplexer_26_out, multiplexer_27_out, multiplexer_28_out,
       multiplexer_29_out, multiplexer_30_out, multiplexer_31_out, multiplexer_32_out, undriven;

  Multiplexer #(.enable("false")) multiplexer_1 (
    .in0(d_flip_flop_1_q), .in1(Input[0]), .out(multiplexer_1_out), .sel(d_flip_flop_17_q));
  Multiplexer #(.enable("false")) multiplexer_2 (
    .in0(d_flip_flop_2_q), .in1(Input[1]), .out(multiplexer_2_out), .sel(d_flip_flop_17_q));
  Multiplexer #(.enable("false")) multiplexer_3 (
    .in0(d_flip_flop_3_q), .in1(Input[2]), .out(multiplexer_3_out), .sel(d_flip_flop_17_q));
  Multiplexer #(.enable("false")) multiplexer_4 (
    .in0(d_flip_flop_4_q), .in1(Input[3]), .out(multiplexer_4_out), .sel(d_flip_flop_17_q));
  Multiplexer #(.enable("false")) multiplexer_5 (
    .in0(d_flip_flop_5_q), .in1(Input[4]), .out(multiplexer_5_out), .sel(d_flip_flop_17_q));
  Multiplexer #(.enable("false")) multiplexer_6 (
    .in0(d_flip_flop_6_q), .in1(Input[5]), .out(multiplexer_6_out), .sel(d_flip_flop_17_q));
  Multiplexer #(.enable("false")) multiplexer_7 (
    .in0(d_flip_flop_7_q), .in1(Input[6]), .out(multiplexer_7_out), .sel(d_flip_flop_17_q));
  Multiplexer #(.enable("false")) multiplexer_8 (
    .in0(d_flip_flop_8_q), .in1(Input[7]), .out(multiplexer_8_out), .sel(d_flip_flop_17_q));
  Multiplexer #(.enable("false")) multiplexer_9 (
    .in0(d_flip_flop_9_q), .in1(Input[8]), .out(multiplexer_9_out), .sel(d_flip_flop_17_q));
  Multiplexer #(.enable("false")) multiplexer_10 (
    .in0(d_flip_flop_10_q), .in1(Input[9]), .out(multiplexer_10_out), .sel(d_flip_flop_17_q));
  Multiplexer #(.enable("false")) multiplexer_11 (
    .in0(d_flip_flop_11_q), .in1(Input[10]), .out(multiplexer_11_out), .sel(d_flip_flop_17_q));
  Multiplexer #(.enable("false")) multiplexer_12 (
    .in0(d_flip_flop_12_q), .in1(Input[11]), .out(multiplexer_12_out), .sel(d_flip_flop_17_q));
  Multiplexer #(.enable("false")) multiplexer_13 (
    .in0(d_flip_flop_13_q), .in1(Input[12]), .out(multiplexer_13_out), .sel(d_flip_flop_17_q));
  Multiplexer #(.enable("false")) multiplexer_14 (
    .in0(d_flip_flop_14_q), .in1(Input[13]), .out(multiplexer_14_out), .sel(d_flip_flop_17_q));
  Multiplexer #(.enable("false")) multiplexer_15 (
    .in0(d_flip_flop_15_q), .in1(Input[14]), .out(multiplexer_15_out), .sel(d_flip_flop_17_q));
  Multiplexer #(.enable("false")) multiplexer_16 (
    .in0(d_flip_flop_16_q), .in1(Input[15]), .out(multiplexer_16_out), .sel(d_flip_flop_17_q));
  Multiplexer #(.enable("false")) multiplexer_17 (
    .in0(d_flip_flop_17_q), .in1(Input[16]), .out(multiplexer_17_out), .sel(d_flip_flop_17_q));
  Multiplexer #(.enable("false")) multiplexer_18 (
    .in0(d_flip_flop_18_q), .in1(Input[17]), .out(multiplexer_18_out), .sel(d_flip_flop_17_q));
  Multiplexer #(.enable("false")) multiplexer_19 (
    .in0(d_flip_flop_19_q), .in1(Input[18]), .out(multiplexer_19_out), .sel(d_flip_flop_17_q));
  Multiplexer #(.enable("false")) multiplexer_20 (
    .in0(d_flip_flop_20_q), .in1(Input[19]), .out(multiplexer_20_out), .sel(d_flip_flop_17_q));
  Multiplexer #(.enable("false")) multiplexer_21 (
    .in0(d_flip_flop_21_p3), .in1(Input[20]), .out(multiplexer_21_out), .sel(d_flip_flop_17_q));
  Multiplexer #(.enable("false")) multiplexer_22 (
    .in0(d_flip_flop_22_q), .in1(Input[21]), .out(multiplexer_22_out), .sel(undriven));
  Multiplexer #(.enable("false")) multiplexer_23 (
    .in0(d_flip_flop_23_q), .in1(Input[22]), .out(multiplexer_23_out), .sel(undriven));
  Multiplexer #(.enable("false")) multiplexer_24 (
    .in0(d_flip_flop_24_q), .in1(Input[23]), .out(multiplexer_24_out), .sel(undriven));
  Multiplexer #(.enable("false")) multiplexer_25 (
    .in0(d_flip_flop_25_q), .in1(Input[24]), .out(multiplexer_25_out), .sel(undriven));
  Multiplexer #(.enable("false")) multiplexer_26 (
    .in0(d_flip_flop_26_q), .in1(Input[25]), .out(multiplexer_26_out), .sel(undriven));
  Multiplexer #(.enable("false")) multiplexer_27 (
    .in0(d_flip_flop_27_q), .in1(Input[26]), .out(multiplexer_27_out), .sel(undriven));
  Multiplexer #(.enable("false")) multiplexer_28 (
    .in0(d_flip_flop_28_q), .in1(Input[27]), .out(multiplexer_28_out), .sel(undriven));
  Multiplexer #(.enable("false")) multiplexer_29 (
    .in0(d_flip_flop_29_q), .in1(Input[28]), .out(multiplexer_29_out), .sel(undriven));
  Multiplexer #(.enable("false")) multiplexer_30 (
    .in0(d_flip_flop_30_q), .in1(Input[29]), .out(multiplexer_30_out), .sel(undriven));
  Multiplexer #(.enable("false")) multiplexer_31 (
    .in0(d_flip_flop_31_q), .in1(Input[30]), .out(multiplexer_31_out), .sel(undriven));
  Multiplexer #(.enable("false")) multiplexer_32 (
    .in0(d_flip_flop_32_q), .in1(Input[31]), .out(multiplexer_32_out), .sel(undriven));
  D_Flip_Flop d_flip_flop_1 (.D(multiplexer_1_out), .Q(d_flip_flop_1_q));  // open: clk, Q_prime
  D_Flip_Flop d_flip_flop_2 (.D(multiplexer_2_out), .Q(d_flip_flop_2_q));  // open: clk, Q_prime
  D_Flip_Flop d_flip_flop_3 (.D(multiplexer_3_out), .Q(d_flip_flop_3_q));  // open: clk, Q_prime
  D_Flip_Flop d_flip_flop_4 (.D(multiplexer_4_out), .Q(d_flip_flop_4_q));  // open: clk, Q_prime
  D_Flip_Flop d_flip_flop_5 (.D(multiplexer_5_out), .Q(d_flip_flop_5_q));  // open: clk, Q_prime
  D_Flip_Flop d_flip_flop_6 (.D(multiplexer_6_out), .Q(d_flip_flop_6_q));  // open: clk, Q_prime
  D_Flip_Flop d_flip_flop_7 (.D(multiplexer_7_out), .Q(d_flip_flop_7_q));  // open: clk, Q_prime
  D_Flip_Flop d_flip_flop_8 (.D(multiplexer_8_out), .Q(d_flip_flop_8_q));  // open: clk, Q_prime
  D_Flip_Flop d_flip_flop_9 (.D(multiplexer_9_out), .Q(d_flip_flop_9_q));  // open: clk, Q_prime
  D_Flip_Flop d_flip_flop_10 (.D(multiplexer_10_out), .Q(d_flip_flop_10_q));  // open: clk, Q_prime
  D_Flip_Flop d_flip_flop_11 (.D(multiplexer_11_out), .Q(d_flip_flop_11_q));  // open: clk, Q_prime
  D_Flip_Flop d_flip_flop_12 (.D(multiplexer_12_out), .Q(d_flip_flop_12_q));  // open: clk, Q_prime
  D_Flip_Flop d_flip_flop_13 (.D(multiplexer_13_out), .Q(d_flip_flop_13_q));  // open: clk, Q_prime
  D_Flip_Flop d_flip_flop_14 (.D(multiplexer_14_out), .clk(clk), .Q(d_flip_flop_14_q));  // open: Q_prime
  D_Flip_Flop d_flip_flop_15 (.D(multiplexer_15_out), .clk(clk), .Q(d_flip_flop_15_q));  // open: Q_prime
  D_Flip_Flop d_flip_flop_16 (.D(multiplexer_16_out), .clk(clk), .Q(d_flip_flop_16_q));  // open: Q_prime
  D_Flip_Flop d_flip_flop_17 (.D(multiplexer_17_out), .clk(clk), .Q(d_flip_flop_17_q));  // open: Q_prime
  D_Flip_Flop d_flip_flop_18 (.D(multiplexer_18_out), .clk(clk), .Q(d_flip_flop_18_q));  // open: Q_prime
  D_Flip_Flop d_flip_flop_19 (.D(multiplexer_19_out), .clk(clk), .Q(d_flip_flop_19_q));  // open: Q_prime
  D_Flip_Flop d_flip_flop_20 (.D(multiplexer_20_out), .clk(clk), .Q(d_flip_flop_20_q));  // open: Q_prime
  // D_Flip_Flop d_flip_flop_21: pin names not known; wires that end beside it: multiplexer_21_out, d_flip_flop_21_p2, d_flip_flop_21_p3
  D_Flip_Flop d_flip_flop_22 (.D(multiplexer_22_out), .clk(d_flip_flop_21_p2), .Q(d_flip_flop_22_q));  // open: Q_prime
  D_Flip_Flop d_flip_flop_23 (.D(multiplexer_23_out), .clk(d_flip_flop_21_p2), .Q(d_flip_flop_23_q));  // open: Q_prime
  D_Flip_Flop d_flip_flop_24 (.D(multiplexer_24_out), .clk(d_flip_flop_21_p2), .Q(d_flip_flop_24_q));  // open: Q_prime
  D_Flip_Flop d_flip_flop_25 (.D(multiplexer_25_out), .clk(d_flip_flop_21_p2), .Q(d_flip_flop_25_q));  // open: Q_prime
  D_Flip_Flop d_flip_flop_26 (.D(multiplexer_26_out), .clk(d_flip_flop_21_p2), .Q(d_flip_flop_26_q));  // open: Q_prime
  D_Flip_Flop d_flip_flop_27 (.D(multiplexer_27_out), .clk(d_flip_flop_21_p2), .Q(d_flip_flop_27_q));  // open: Q_prime
  D_Flip_Flop d_flip_flop_28 (.D(multiplexer_28_out), .clk(d_flip_flop_21_p2), .Q(d_flip_flop_28_q));  // open: Q_prime
  D_Flip_Flop d_flip_flop_29 (.D(multiplexer_29_out), .clk(d_flip_flop_21_p2), .Q(d_flip_flop_29_q));  // open: Q_prime
  D_Flip_Flop d_flip_flop_30 (.D(multiplexer_30_out), .clk(d_flip_flop_21_p2), .Q(d_flip_flop_30_q));  // open: Q_prime
  D_Flip_Flop d_flip_flop_31 (.D(multiplexer_31_out), .clk(d_flip_flop_21_p2), .Q(d_flip_flop_31_q));  // open: Q_prime
  D_Flip_Flop d_flip_flop_32 (.D(multiplexer_32_out), .clk(d_flip_flop_21_p2), .Q(d_flip_flop_32_q));  // open: Q_prime
endmodule
